# Fritzing sketch v1.0 (saved by Fritzing 0.9.4)
circuit board: 2.95062cm x 3.9908cm
breadboards: 1

parts:
  U1 = atmega328 [package=dip]
  S1 = Toggle Switch [package=THT]
  R1 = Resistor [tolerance=±5% resistance=220 package=THT]
  C3 = Ceramic Capacitor [capacitance=100nF package="100 mil [THT, multilayer]"]
  C4 = Electrolytic Capacitor [capacitance=1µF package="100 mil [THT, electrolytic]"]
  Q2 = NPN-Transistor [package="TO92 [THT]"]
  R3 = Resistor [tolerance=±5% resistance=220 package=THT]
  L1 = Solenoid
  JP1 = Header 2 [package=jst-2-pth-ns]
  JP2 = Header 2 [package=jst-2-pth-ns]

nets:
  N1: U1.RESET, S1.L1
  N2: U1.D0_(RX), S1.COM
  N3: U1.D1_(TX), S1.L2
  N4: U1.D2, R1.Pin_1
  N5: U1.VCC, C3.1, C4.+, L1.pin1, JP2.2
  N6: U1.GND, C3.0, C4.-, Q2.E, JP1.1
  N7: U1.D6_(PWM), R3.Pin_0
  N8: U1.D8, R1.Pin_0, JP1.2
  N9: Q2.B, R3.Pin_1
  N10: Q2.C, L1.pin2

notes:
  Solenoid
  BLA GRE
  2N2222
  1k
  22k
  RST
  RX
  TX
  1μF
  5v
  GND
  RED YEL
  Sentry Safe Fixed Board v1.0
  Etienne
  Sellan
  2022
  ATmega328
