# Fritzing sketch v2.0 (saved by Fritzing 0.9.4)
circuit board: 2.95062cm x 4.07125cm
breadboards: 1

parts:
  U1 = atmega328 [package=dip]
  S1 = Toggle Switch [package=THT]
  R1 = Resistor [tolerance=±5% resistance=220 package=THT]
  C4 = Electrolytic Capacitor [capacitance=1µF package="100 mil [THT, electrolytic]"]
  Q2 = NPN-Transistor [package="TO92 [THT]"]
  R3 = Resistor [tolerance=±5% resistance=220 package=THT]
  L1 = Solenoid
  JP1 = Header 2 [package=jst-2-pth-ns]
  JP2 = Header 2 [package=jst-2-pth-ns]
  Espessif_Serial_Wifi_Modul_1 = ESP8266 ESP01 [part_number=ESP8266 package=THT]
  VCC1 = Battery
  Q3 = NPN-Transistor [package="TO92 [THT]"]
  R4 = Resistor [tolerance=±5% resistance=220 package=THT]
  R5 = Resistor [tolerance=±5% resistance=220 package=THT]

nets:
  N1: U1.RESET, S1.L1
  N2: U1.D0_(RX), S1.COM, Espessif_Serial_Wifi_Modul_1.TXD
  N3: U1.D1_(TX), S1.L2, Espessif_Serial_Wifi_Modul_1.RXD
  N4: U1.D2, R1.Pin_0
  N5: U1.D3_(PWM), R4.Pin_0
  VCC: U1.VCC, C4.+, L1.pin1, JP2.2, Espessif_Serial_Wifi_Modul_1.VCC, VCC1.+, R5.Pin_1
  N6: U1.GND, C4.-, Q2.E, JP1.1, VCC1.-, Q3.E
  N7: U1.D6_(PWM), R3.Pin_0
  N8: U1.D8, R1.Pin_1, JP1.2
  N9: Q2.B, R3.Pin_1
  N10: Q2.C, L1.pin2
  N11: Espessif_Serial_Wifi_Modul_1.GND, Q3.C
  N12: Espessif_Serial_Wifi_Modul_1.CH_PD, R5.Pin_0
  N13: Q3.B, R4.Pin_1

notes:
  Solenoid
  BLA GRE
  2N2222
  1k
  22k
  RST
  RX
  TX
  1μF
  5v
  GND
  RED YEL
  Sentry Safe Fixed Board v2.0
  ATmega328
  ESP01
  Etienne Sellan - 2022
  10k

custom parts:
  ESP8266 ESP01: Generic WiFi Module based on the ESP8266 with onboard PCB antenna and UART communications
